// Logisim project s-mips.circ as structural Verilog
module S_MIPS_Board (
  input  DESHABILITAR_DISPATCHER,
  output halt
);

  wire button_1_out, CLK, CS, d_ff_1_q, LCLR, LoadRAM, LoadRAMOn, LW, R_R_W, R_W, ram_dispatcher_1_finished,
       RCS, Reset_out, RST, TTY_EN;
  wire [2:0] KDB;
  wire [3:0] LMask, Mask, ram_1_read_time, ram_1_write_time, RMask;
  wire [6:0] KDB_DATA, TTY_DATA;
  wire [15:0] Addr, LAddr, RAddr;
  wire [31:0] I0, I1, I2, I3, LData, ram_1_data_out_0, ram_1_data_out_1, ram_1_data_out_2, ram_1_data_out_3,
       RI0, RI1, RI2, RI3;

  TTY #(.rows(25), .cols(80)) tty_1 (.data(TTY_DATA), .clk(CLK), .we(TTY_EN), .clr(RST));
  not not_1 (LoadRAMOn, ram_dispatcher_1_finished);
  RAM_Dispatcher ram_dispatcher_1 (
    .WriteTime(ram_1_write_time), .Clock(CLK), .Data(LData), .Address(LAddr), .Mask(LMask),
    .Finished(ram_dispatcher_1_finished), .Write(LW), .CLR(LCLR));
  Keyboard #(.buflen(64)) keyboard_1 (.clk(CLK), .re(KDB[0]), .avail(KDB[2]), .data(KDB_DATA));  // open: clr
  RAM ram_1 (
    .Address(RAddr), .Data_Out_0(ram_1_data_out_0), .Data_Out_1(ram_1_data_out_1),
    .Data_Out_2(ram_1_data_out_2), .Data_Out_3(ram_1_data_out_3), .Data_In_0(RI0), .Data_In_1(RI1),
    .Data_In_2(RI2), .Data_In_3(RI3), .Mask(RMask), .nRead_Write(R_R_W), .Chip_Select(RCS),
    .Read_Time(ram_1_read_time), .Reset(button_1_out), .Write_Time(ram_1_write_time));
  Button button_1 (.out(button_1_out));
  D_Flip_Flop d_ff_1 (.clk(CLK), .D(1'b1), .Q(d_ff_1_q), .reset(Reset_out));  // open: Qn, preset, en
  Button Reset (.out(Reset_out));
  S_MIPS s_mips_1 (
    .Kbd_Enable(KDB[0]), .Address(Addr), .Kbd_Clear(KDB[1]), .Kbd_Available(KDB[2]), .RAM_In_0(I0),
    .Kbd_ASCII_Data(KDB_DATA), .RAM_In_1(I1), .TTY_Enable(TTY_EN), .RAM_In_2(I2), .RAM_In_3(I3),
    .TTY_ASCII_Data(TTY_DATA), .Reset(RST), .RAM_Out_0(ram_1_data_out_0), .RAM_Out_1(ram_1_data_out_1),
    .Stop(halt), .RAM_Out_2(ram_1_data_out_2), .RAM_Out_3(ram_1_data_out_3), .Mask(Mask),
    .Read_Time(ram_1_read_time), .Write_Time(ram_1_write_time), .nRead_Write(R_W), .Chip_Select(CS),
    .Clock(CLK));
  D_Flip_Flop d_ff_2 (.clk(CLK), .D(d_ff_1_q), .Qn(LCLR), .reset(Reset_out));  // open: Q, preset, en
  or or_1 (RST, LCLR, LoadRAM);
  Clock clock_1 (.out(CLK));
  Multiplexer #(.width(32), .enable("false")) multiplexer_1 (.in0(I0), .in1(LData), .out(RI0), .sel(LoadRAM));
  Multiplexer #(.width(32), .enable("false")) multiplexer_2 (.in0(I1), .in1(LData), .out(RI1), .sel(LoadRAM));
  Multiplexer #(.width(32), .enable("false")) multiplexer_3 (.in0(I2), .in1(LData), .out(RI2), .sel(LoadRAM));
  Multiplexer #(.width(32), .enable("false")) multiplexer_4 (.in0(I3), .in1(LData), .out(RI3), .sel(LoadRAM));
  and and_1 (LoadRAM, ~DESHABILITAR_DISPATCHER, LoadRAMOn);  // AND_Gate
  Multiplexer #(.width(16), .enable("false")) multiplexer_5 (.in0(Addr), .in1(LAddr), .out(RAddr), .sel(LoadRAM));
  Multiplexer #(.width(4), .enable("false")) multiplexer_6 (.in0(Mask), .in1(LMask), .out(RMask), .sel(LoadRAM));
  Multiplexer #(.enable("false")) multiplexer_7 (.in0(CS), .in1(LW), .out(RCS), .sel(LoadRAM));
  Multiplexer #(.enable("false")) multiplexer_8 (.in0(R_W), .in1(LW), .out(R_R_W), .sel(LoadRAM));

  // Notes on the sheet:
  //   NO MODIFICAR
  //   Keyboard
endmodule

module RAM (
  input  [15:0] Address,
  input  [31:0] Data_In_0,
  input  [31:0] Data_In_1,
  input  [31:0] Data_In_2,
  input  [31:0] Data_In_3,
  input  [3:0] Mask,
  input  nRead_Write,
  input  Chip_Select,
  input  Reset,
  output [31:0] Data_Out_0,
  output [31:0] Data_Out_1,
  output [31:0] Data_Out_2,
  output [31:0] Data_Out_3,
  output [3:0] Read_Time,
  output [3:0] Write_Time
);

  wire and_2_out, and_3_out, and_4_out, and_5_out, and_6_out, and_7_out, and_8_out, and_9_out, Changed, CLK,
       comparator_2_eq, comparator_3_eq, comparator_4_eq, comparator_5_eq, comparator_6_eq, Count,
       demultiplexer_3_out0, Idle, Idle_q, Load, Load0, Load1, nand_1_out, or_1_out, or_2_out, or_3_out,
       or_4_out, or_5_out, or_6_out, or_7_out, or_8_out, or_9_out, or_10_out, Proc_q, Update_Mem, Zero_Time;
  wire [3:0] counter_1_q, multiplexer_1_out, subtractor_1_out;
  wire [31:0] register_1_q, register_2_q, register_3_q, register_4_q, register_5_q;

  // Probe on 4'b0011
  // Probe on 4'b0010
  Multiplexer #(.width(4), .enable("false")) multiplexer_1 (
    .in0(4'b0011), .in1(4'b0010), .out(multiplexer_1_out), .sel(nRead_Write));
  or or_1 (or_1_out, Idle, Update_Mem);
  or or_2 (or_2_out, ~Chip_Select, Reset);  // OR_Gate
  Subtractor #(.width(4)) subtractor_1 (.a(multiplexer_1_out), .b(4'b0010), .out(subtractor_1_out));  // open: bin, bout
  D_Flip_Flop u_Idle (.clk(CLK), .D(or_1_out), .Q(Idle_q), .preset(or_2_out));  // open: Qn, en, reset
  Demultiplexer #(.enable("false")) demultiplexer_1 (.out0(Idle), .out1(Load0), .in(Idle_q), .sel(Changed));
  // Probe on counter_1_q
  Counter #(.width(4), .max('hf)) counter_1 (
    .load(Load), .D(subtractor_1_out), .count(Count), .Q(counter_1_q), .clk(CLK), .clr(or_3_out));  // open: carry
  or or_3 (or_3_out, ~Chip_Select, Reset);  // OR_Gate
  Comparator #(.width(4), .mode("unsigned")) comparator_1 (
    .a(4'b0000), .b(counter_1_q), .eq(Zero_Time));  // open: gt, lt
  or or_4 (or_4_out, Count, Load0, Load1);
  Register #(.width(32)) register_1 (.D(Data_In_0), .en(Chip_Select), .Q(register_1_q), .clk(CLK), .clr(or_5_out));
  or or_5 (or_5_out, ~Chip_Select, Reset);  // OR_Gate
  Register #(.width(32)) register_2 (.D(Data_In_1), .en(Chip_Select), .Q(register_2_q), .clk(CLK), .clr(or_6_out));
  or or_6 (or_6_out, ~Chip_Select, Reset);  // OR_Gate
  Register #(.width(32)) register_3 (.D(Data_In_2), .en(Chip_Select), .Q(register_3_q), .clk(CLK), .clr(or_7_out));
  or or_7 (or_7_out, ~Chip_Select, Reset);  // OR_Gate
  Register #(.width(32)) register_4 (.D(Data_In_3), .en(Chip_Select), .Q(register_4_q), .clk(CLK), .clr(or_8_out));
  or or_8 (or_8_out, ~Chip_Select, Reset);  // OR_Gate
  Register #(.width(32)) register_5 (
    .D({{11{1'b1}}, nRead_Write, Mask, Address}), .en(Chip_Select), .Q(register_5_q), .clk(CLK),
    .clr(or_9_out));
  or or_9 (or_9_out, ~Chip_Select, Reset);  // OR_Gate
  D_Flip_Flop Proc (.clk(CLK), .D(or_4_out), .Q(Proc_q), .reset(or_10_out));  // open: Qn, preset, en
  or or_10 (or_10_out, ~Chip_Select, Reset);  // OR_Gate
  Demultiplexer #(.enable("false")) demultiplexer_2 (
    .out0(Count), .out1(Update_Mem), .in(demultiplexer_3_out0), .sel(Zero_Time));
  Demultiplexer #(.enable("false")) demultiplexer_3 (
    .out0(demultiplexer_3_out0), .out1(Load1), .in(Proc_q), .sel(Changed));
  Clock clock_1 (.out(CLK));
  Comparator #(.width(32)) comparator_2 (.a(register_1_q), .b(Data_In_0), .eq(comparator_2_eq));  // open: gt, lt
  Comparator #(.width(32)) comparator_3 (.a(register_2_q), .b(Data_In_1), .eq(comparator_3_eq));  // open: gt, lt
  Comparator #(.width(32)) comparator_4 (.a(register_3_q), .b(Data_In_2), .eq(comparator_4_eq));  // open: gt, lt
  Comparator #(.width(32)) comparator_5 (.a(register_4_q), .b(Data_In_3), .eq(comparator_5_eq));  // open: gt, lt
  Comparator #(.width(32)) comparator_6 (
    .a(register_5_q), .b({{11{1'b1}}, nRead_Write, Mask, Address}), .eq(comparator_6_eq));  // open: gt, lt
  nand nand_1 (nand_1_out, comparator_6_eq, comparator_2_eq, comparator_3_eq, comparator_4_eq, comparator_5_eq);
  and and_1 (Changed, nand_1_out, Chip_Select);
  or or_11 (Load, Count, Load1, Load0);
  and and_2 (and_2_out, Mask[0], Update_Mem, nRead_Write);
  and and_3 (and_3_out, Mask[1], Update_Mem, nRead_Write);
  and and_4 (and_4_out, Mask[2], Update_Mem, nRead_Write);
  and and_5 (and_5_out, Mask[3], Update_Mem, nRead_Write);
  RAM_part #(.addrWidth(16), .dataWidth(32), .bus("separate")) ram_1 (
    .addr(Address), .din(Data_In_0), .data(Data_Out_0), .str(and_2_out), .sel(Chip_Select), .clk(CLK),
    .ld(and_6_out), .clr(Reset));
  and and_6 (and_6_out, ~nRead_Write, Idle);  // AND_Gate
  RAM_part #(.addrWidth(16), .dataWidth(32), .bus("separate")) ram_2 (
    .addr(Address), .din(Data_In_1), .data(Data_Out_1), .str(and_3_out), .sel(Chip_Select), .clk(CLK),
    .ld(and_7_out), .clr(Reset));
  and and_7 (and_7_out, ~nRead_Write, Idle);  // AND_Gate
  RAM_part #(.addrWidth(16), .dataWidth(32), .bus("separate")) ram_3 (
    .addr(Address), .din(Data_In_2), .data(Data_Out_2), .str(and_4_out), .sel(Chip_Select), .clk(CLK),
    .ld(and_8_out), .clr(Reset));
  and and_8 (and_8_out, ~nRead_Write, Idle);  // AND_Gate
  RAM_part #(.addrWidth(16), .dataWidth(32), .bus("separate")) ram_4 (
    .addr(Address), .din(Data_In_3), .data(Data_Out_3), .str(and_5_out), .sel(Chip_Select), .clk(CLK),
    .ld(and_9_out), .clr(Reset));
  and and_9 (and_9_out, ~nRead_Write, Idle);  // AND_Gate

  assign Read_Time = 4'b0011;
  assign Write_Time = 4'b0010;

  // Other names for the same wires on the sheet: M0 = Mask[0]; M1 = Mask[1]; M2 = Mask[2]; M3 = Mask[3];
  //   RW = nRead_Write; CLR = Reset; CS = Chip_Select; Load2 = Count

  // Notes on the sheet:
  //   NO MODIFICAR
  //   excepto quizás los valores RT y WT
  //   BANK0
  //   BANK1
  //   BANK2
  //   BANK3
endmodule

module S_MIPS (
  input  [31:0] RAM_Out_0,
  input  [31:0] RAM_Out_1,
  input  [31:0] RAM_Out_2,
  input  [31:0] RAM_Out_3,
  input  [3:0] Read_Time,
  input  [3:0] Write_Time,
  input  Kbd_Available,
  input  [6:0] Kbd_ASCII_Data,
  input  Reset,
  input  Clock,
  output [15:0] Address,
  output [31:0] RAM_In_0,
  output [31:0] RAM_In_1,
  output [31:0] RAM_In_2,
  output [31:0] RAM_In_3,
  output [3:0] Mask,
  output nRead_Write,
  output Chip_Select,
  output Kbd_Enable,
  output Kbd_Clear,
  output TTY_Enable,
  output [6:0] TTY_ASCII_Data,
  output Stop
);

  wire add, addi, \and , and_3_out, and_7_out, and_9_out, andi, beq, bgtz, blez, bltz, bne, cond, \continue ,
       CS_RI, CS_Rlw, CS_Rpop, CS_W, demultiplexer_1_out0, demultiplexer_1_out1, demultiplexer_3_out1,
       demultiplexer_3_out2, demultiplexer_5_out0, demultiplexer_5_out1, div, divu, halt, IDLE_q, insEn, j,
       jr, kbd, lw, mfhi, mflo, mult, mulu, nop, \nor , not_1_out, not_2_out, not_3_out, not_4_out,
       not_5_out, not_6_out, not_7_out, not_8_out, not_9_out, not_10_out, not_11_out, not_12_out, \or ,
       or_1_out, or_2_out, or_3_out, or_4_out, or_5_out, or_6_out, or_7_out, or_8_out, or_9_out, or_10_out,
       or_11_out, or_12_out, or_13_out, or_14_out, or_16_out, or_17_out, or_20_out, or_21_out, or_22_out,
       or_25_out, or_26_out, or_28_out, or_29_out, or_30_out, or_31_out, or_32_out, or_33_out, or_34_out,
       or_35_out, or_36_out, ori, pop, push, RDW, Read_Instr_End, reading, Reading_End_lw, Reading_End_pop,
       ready, ready0, ready1, ready2, ready3, Ret, Ret_to_RI, Ret_to_Rlw, Ret_to_Rpop, Ret_to_W, Ret_to_WP,
       Ret_to_WR, RI, RI_end, rnd, RTW, slt, slti, sltiu, sltu, sub, sw, tty, waitPop, waitRead, WE3, WP_end,
       WP_q, WR_end, WR_q, Writing_End, \xor , xori;
  wire [1:0] and_8_out, bit_extender_4_out, bit_extender_5_out, Offset, ReadOffset, selector;
  wire [2:0] ALU_OP;
  wire [3:0] counter_1_q, counter_2_q, counter_3_q, counter_4_q, counter_5_q, counter_6_q, counter_7_q;
  wire [4:0] multiplexer_3_out, multiplexer_4_out, RD, RS, RT;
  wire [15:0] Const, multiplexer_14_out, Read_Address, Read_Ins_Address, Write_Address;
  wire [25:0] Destiny_jump;
  wire [31:0] adder_1_out, adder_2_out, adder_3_out, ALU_OUT, bit_extender_1_out, bit_extender_2_out,
       bit_extender_3_out, bit_extender_6_out, bit_extender_7_out, Curr_PC, ExtendedConst, HI, instruction,
       Key_Value, LO, memory_reader_1_instruction, multiplexer_2_out, multiplexer_5_out, multiplexer_6_out,
       multiplexer_8_out, multiplexer_9_out, multiplexer_11_out, multiplexer_12_out, multiplexer_16_out,
       multiplexer_17_out, multiplier_1_out, New_PC, random, RD2, Readed_Value, RF_In, SP, subtractor_1_out;
  wire [31:7] RD1;

  assign bit_extender_1_out = {{25{1'b0}}, Kbd_ASCII_Data};  // Bit_Extender bit_extender_1
  not not_1 (not_1_out, Kbd_Available);
  Multiplexer #(.width(32)) multiplexer_1 (
    .in0(bit_extender_1_out), .in1({32{1'b1}}), .out(Key_Value), .sel(not_1_out));  // open: en
  Multiplexer #(.width(32)) multiplexer_2 (
    .in0(RD2), .in1(ExtendedConst), .out(multiplexer_2_out), .sel(or_1_out));  // open: en
  or or_1 (or_1_out, RTW, sw);
  Program_Counter program_counter_1 (
    .Clock(Clock), .Reset(Reset), .PC_ENABLE(ready), .Next_Address(New_PC), .Current_Address(Curr_PC));
  or or_2 (or_2_out, ready3, ready2);
  and and_1 (cond, ~ready3, RTW);  // AND_Gate
  Memory_Reader memory_reader_1 (
    .Current_Address(Curr_PC), .RAM_OUT_0(RAM_Out_0), .RAM_OUT_1(RAM_Out_1), .RAM_OUT_2(RAM_Out_2),
    .RAM_OUT_3(RAM_Out_3), .Address(Read_Ins_Address), .Instruction(memory_reader_1_instruction));
  Decoder decoder_1 (
    .in_1(instruction), .div(div), .add(add), .nop(nop), .tty(tty), .mfhi(mfhi), .mflo(mflo), .xori(xori),
    .andi(andi), .slti(slti), .sltiu(sltiu), .lw(lw), .sw(sw), .mult(mult), .sub(sub), .mulu(mulu),
    .pop(pop), .rnd(rnd), .push(push), .divu(divu), .slt(slt), .ori(ori), .addi(addi), .beq(beq), .bne(bne),
    .\nor (\nor ), .\xor (\xor ), .\or (\or ), .\and (\and ), .sltu(sltu), .bltz(bltz), .j(j), .blez(blez),
    .bgtz(bgtz), .halt(halt), .kbd(kbd), .ALU_OP(ALU_OP), .WE3(WE3), .RD(RD), .RT(RT), .RS(RS),
    .Const(Const), .Destiny_Jump(Destiny_jump), .jr(jr));
  or or_3 (or_3_out, WE3, kbd, or_2_out);
  or or_4 (or_4_out, or_2_out, ready1);
  ALU alu_1 (
    .A({RD1, TTY_ASCII_Data}), .B(multiplexer_2_out), .ALUOP(ALU_OP), .Clock(Clock), .Reset(Reset),
    .mult(mult), .mulu(mulu), .div(div), .divu(divu), .ready(ready1), .HI(HI), .ALU_Result(ALU_OUT), .LO(LO));
  Register #(.width(32)) register_1 (
    .D(memory_reader_1_instruction), .en(Read_Instr_End), .Q(instruction), .clk(Clock), .clr(Reset));
  Multiplexer #(.width(5)) multiplexer_3 (
    .in0(5'b10001), .in1(RD), .out(multiplexer_3_out), .sel(or_5_out));  // open: en
  or or_5 (or_5_out, RDW, ready3);
  and and_2 (Kbd_Clear, halt, ready1);
  and and_3 (and_3_out, push, ready0);
  Multiplexer #(.width(5)) multiplexer_4 (
    .in0(multiplexer_3_out), .in1(RT), .out(multiplexer_4_out), .sel(or_6_out));  // open: en
  or or_6 (or_6_out, cond, ready2);
  and and_4 (Stop, halt, ready1);
  Register_File register_file_1 (
    .WD3(RF_In), .clock(Clock), .Reset(Reset), .RD1({RD1, TTY_ASCII_Data}), .RD2(RD2),
    .A3(multiplexer_4_out), .A1(RS), .A2(RT), .SP(SP), .Update_Push(and_3_out), .ready(or_3_out),
    .WE3(or_4_out), .upop(ready3));
  and and_5 (TTY_Enable, tty, ready1);
  or or_7 (or_7_out, demultiplexer_1_out0, ready);
  Multiplier #(.width(32)) multiplier_1 (.a(Curr_PC), .b(32'h64), .out(multiplier_1_out));  // open: cin, cout
  Demultiplexer demultiplexer_1 (
    .out0(demultiplexer_1_out0), .out1(demultiplexer_1_out1), .in(IDLE_q), .sel(not_2_out));  // open: en
  D_Flip_Flop IDLE (.clk(Clock), .D(or_7_out), .Q(IDLE_q), .preset(Reset));  // open: Qn, en, reset
  or or_8 (or_8_out, ready2, ready3);
  assign bit_extender_2_out = {{16{1'b0}}, Const};  // Bit_Extender bit_extender_2
  assign bit_extender_3_out = {{16{Const[15]}}, Const};  // Bit_Extender bit_extender_3
  Adder #(.width(32)) adder_1 (.a(multiplier_1_out), .b(32'hc), .out(adder_1_out));  // open: cin, cout
  and and_6 (Kbd_Enable, kbd, ready1);
  not not_2 (not_2_out, or_9_out);
  or or_9 (or_9_out, reading, CS_W);
  Multiplexer #(.width(32)) multiplexer_5 (.in0(ALU_OUT), .in1(HI), .out(multiplexer_5_out), .sel(mfhi));  // open: en
  or or_10 (or_10_out, mflo, ready2, ready3);
  Multiplexer #(.width(32)) multiplexer_6 (
    .in0(LO), .in1(Readed_Value), .out(multiplexer_6_out), .sel(or_8_out));  // open: en
  Multiplexer #(.width(32)) multiplexer_7 (
    .in0(bit_extender_2_out), .in1(bit_extender_3_out), .out(ExtendedConst), .sel(not_3_out));  // open: en
  not not_3 (not_3_out, andi);
  Branch_Control branch_control_1 (
    .RS({RD1, TTY_ASCII_Data}), .RT(RD2), .Current_Address(Curr_PC), .Const(Const),
    .DestinyJump(Destiny_jump), .beq(beq), .bne(bne), .blez(blez), .bgtz(bgtz), .bltz(bltz), .j(j), .jr(jr),
    .New_Address(New_PC));
  or or_11 (or_11_out, Ret_to_RI, demultiplexer_1_out1);
  Multiplexer #(.width(32)) multiplexer_8 (
    .in0(multiplexer_5_out), .in1(multiplexer_6_out), .out(multiplexer_8_out), .sel(or_10_out));  // open: en
  not not_4 (not_4_out, or_12_out);
  or or_12 (or_12_out, ready2, ready3);
  Multiplier #(.width(32)) multiplier_2 (.a(adder_1_out), .b(32'hc8), .out(random));  // open: cin, cout
  Counter #(.width(4), .max('hf)) counter_1 (
    .Q(counter_1_q), .clk(Clock), .clr(or_13_out));  // open: load, D, count, carry
  or or_13 (or_13_out, Reset, not_5_out);
  D_Flip_Flop Reading_Instruction (.clk(Clock), .D(or_11_out), .Q(CS_RI), .reset(Reset));  // open: Qn, preset, en
  or or_14 (or_14_out, sw, push);
  or or_15 (RDW, add, sub, \and , \or , \nor , \xor , slt, sltu, mfhi, mflo, rnd, kbd);
  and and_7 (and_7_out, not_4_out, rnd);
  not not_5 (not_5_out, CS_RI);
  or or_16 (or_16_out, lw, pop);
  assign bit_extender_4_out = {{1{1'b0}}, or_16_out};  // Bit_Extender bit_extender_4
  assign bit_extender_5_out = {{1{or_14_out}}, or_14_out};  // Bit_Extender bit_extender_5
  Multiplexer #(.width(32)) multiplexer_9 (
    .in0(multiplexer_8_out), .in1(random), .out(multiplexer_9_out), .sel(and_7_out));  // open: en
  not not_6 (not_6_out, or_17_out);
  or or_17 (or_17_out, ready2, ready3);
  Comparator #(.width(4), .mode("unsigned")) comparator_1 (
    .a(counter_1_q), .b(Read_Time), .eq(Read_Instr_End));  // open: gt, lt
  Demultiplexer demultiplexer_2 (.out0(Ret_to_RI), .out1(RI), .in(CS_RI), .sel(Read_Instr_End));  // open: en
  assign selector = bit_extender_4_out | and_8_out | 2'b00;  // OR_Gate or_18, 2 bits wide
  assign and_8_out = bit_extender_5_out & 2'b10;  // AND_Gate and_8, 2 bits wide
  Multiplexer #(.width(32)) multiplexer_10 (
    .in0(multiplexer_9_out), .in1(Key_Value), .out(RF_In), .sel(and_9_out));  // open: en
  and and_9 (and_9_out, not_6_out, kbd);
  Adder #(.width(32)) adder_2 (
    .a({RD1, TTY_ASCII_Data}), .b(bit_extender_6_out), .out(adder_2_out));  // open: cin, cout
  assign bit_extender_6_out = {{16{Const[15]}}, Const};  // Bit_Extender bit_extender_6
  Multiplexer #(.select(2), .width(32)) multiplexer_11 (
    .in0(RAM_Out_0), .in1(RAM_Out_1), .in2(RAM_Out_2), .in3(RAM_Out_3), .out(multiplexer_11_out), .sel(Offset));  // open: en
  Demultiplexer #(.select(2)) demultiplexer_3 (
    .out0(ready1), .out1(demultiplexer_3_out1), .out2(demultiplexer_3_out2), .in(\continue ), .sel(selector));  // open: out3, en
  or or_19 (Chip_Select, CS_RI, CS_W, CS_Rlw, CS_Rpop);
  Multiplexer #(.width(32)) multiplexer_12 (
    .in0(adder_2_out), .in1(SP), .out(multiplexer_12_out), .sel(pop));  // open: en
  MemoryReaderNOI memoryreadernoi_1 (.Address_To_Read(multiplexer_12_out), .Address(Read_Address), .OffSet(ReadOffset));
  or or_20 (or_20_out, demultiplexer_3_out2, Ret_to_W);
  Register #(.width(32)) register_2 (
    .D(multiplexer_11_out), .en(or_21_out),
    .Q({Readed_Value[7:0], Readed_Value[15:8], Readed_Value[23:16], Readed_Value[31:24]}), .clk(Clock));  // open: clr
  or or_21 (or_21_out, Reading_End_pop, Reading_End_lw);
  Counter #(.width(4), .max('hf)) counter_2 (
    .Q(counter_2_q), .clk(Clock), .clr(or_22_out));  // open: load, D, count, carry
  or or_22 (or_22_out, Reset, not_7_out);
  not not_7 (not_7_out, CS_W);
  D_Flip_Flop Writing (.clk(Clock), .D(or_20_out), .Q(CS_W), .reset(Reset));  // open: Qn, preset, en
  Multiplexer multiplexer_13 (.in0(1'b0), .in1(1'b1), .out(nRead_Write), .sel(CS_W));  // open: en
  Multiplexer #(.width(16)) multiplexer_14 (
    .in0(Read_Ins_Address), .in1(Write_Address), .out(multiplexer_14_out), .sel(CS_W));  // open: en
  Demultiplexer demultiplexer_4 (.out0(Ret_to_W), .out1(ready0), .in(CS_W), .sel(Writing_End));  // open: en
  or or_23 (ready, ready3, ready0, ready2, ready1);
  or or_24 (RTW, addi, andi, ori, xori, slti, sltiu);
  Register #(.width(2)) register_3 (.D(ReadOffset), .Q(Offset), .clk(or_25_out));  // open: en, clr
  or or_25 (or_25_out, Reading_End_pop, Reading_End_lw);
  Comparator #(.width(4), .mode("unsigned")) comparator_2 (
    .a(counter_2_q), .b(Write_Time), .eq(Writing_End));  // open: gt, lt
  Multiplexer #(.width(16)) multiplexer_15 (
    .in0(multiplexer_14_out), .in1(Read_Address), .out(Address), .sel(reading));  // open: en
  Demultiplexer demultiplexer_5 (
    .out0(demultiplexer_5_out0), .out1(demultiplexer_5_out1), .in(demultiplexer_3_out1), .sel(lw));  // open: en
  assign bit_extender_7_out = {{16{Const[15]}}, Const};  // Bit_Extender bit_extender_7
  Subtractor #(.width(32)) subtractor_1 (.a(SP), .b(32'h4), .out(subtractor_1_out));  // open: bin, bout
  Adder #(.width(32)) adder_3 (
    .a({RD1, TTY_ASCII_Data}), .b(bit_extender_7_out), .out(adder_3_out));  // open: cin, cout
  or or_26 (or_26_out, demultiplexer_5_out1, Ret_to_Rlw);
  or or_27 (reading, CS_Rlw, CS_Rpop);
  Multiplexer #(.width(32)) multiplexer_16 (
    .in0(adder_3_out), .in1(subtractor_1_out), .out(multiplexer_16_out), .sel(push));  // open: en
  Counter #(.width(4), .max('hf)) counter_3 (
    .Q(counter_3_q), .clk(Clock), .clr(or_28_out));  // open: load, D, count, carry
  or or_28 (or_28_out, Reset, not_9_out);
  or or_29 (or_29_out, demultiplexer_5_out0, Ret_to_Rpop);
  Counter #(.width(4), .max('hf)) counter_4 (
    .Q(counter_4_q), .clk(Clock), .clr(or_30_out));  // open: load, D, count, carry
  or or_30 (or_30_out, Reset, not_8_out);
  not not_8 (not_8_out, CS_Rlw);
  D_Flip_Flop Reading_lw (.clk(Clock), .D(or_26_out), .Q(CS_Rlw), .reset(Reset));  // open: Qn, preset, en
  Multiplexer #(.width(32)) multiplexer_17 (
    .in0(RD2), .in1({RD1, TTY_ASCII_Data}), .out(multiplexer_17_out), .sel(push));  // open: en
  not not_9 (not_9_out, CS_Rpop);
  D_Flip_Flop Reading_pop (.clk(Clock), .D(or_29_out), .Q(CS_Rpop), .reset(Reset));  // open: Qn, preset, en
  Memory_Writer memory_writer_1 (
    .Data_In(multiplexer_17_out), .Address_In(multiplexer_16_out), .Data_In_0(RAM_In_0),
    .Data_In_1(RAM_In_1), .Data_In_2(RAM_In_2), .Data_In_3(RAM_In_3), .Address(Write_Address), .mask(Mask));
  Comparator #(.width(4), .mode("unsigned")) comparator_3 (
    .a(counter_3_q), .b(Read_Time), .eq(Reading_End_pop));  // open: gt, lt
  Demultiplexer demultiplexer_6 (.out0(Ret_to_Rpop), .out1(waitPop), .in(CS_Rpop), .sel(Reading_End_pop));  // open: en
  Comparator #(.width(4), .mode("unsigned")) comparator_4 (
    .a(counter_4_q), .b(Read_Time), .eq(Reading_End_lw));  // open: gt, lt
  Demultiplexer demultiplexer_7 (.out0(Ret_to_Rlw), .out1(waitRead), .in(CS_Rlw), .sel(Reading_End_lw));  // open: en
  or or_31 (or_31_out, RI, Ret);
  or or_32 (or_32_out, Ret_to_WR, waitRead);
  or or_33 (or_33_out, Ret_to_WP, waitPop);
  Counter #(.width(4), .max('hf)) counter_5 (
    .Q(counter_5_q), .clk(Clock), .clr(or_34_out));  // open: load, D, count, carry
  or or_34 (or_34_out, Reset, not_12_out);
  D_Flip_Flop u_RI (.clk(Clock), .D(or_31_out), .Q(insEn), .reset(Reset));  // open: Qn, preset, en
  Counter #(.width(4), .max('hf)) counter_6 (
    .Q(counter_6_q), .clk(Clock), .clr(or_35_out));  // open: load, D, count, carry
  or or_35 (or_35_out, Reset, not_10_out);
  not not_10 (not_10_out, WR_q);
  D_Flip_Flop WR (.clk(Clock), .D(or_32_out), .Q(WR_q), .reset(Reset));  // open: Qn, preset, en
  Counter #(.width(4), .max('hf)) counter_7 (
    .Q(counter_7_q), .clk(Clock), .clr(or_36_out));  // open: load, D, count, carry
  or or_36 (or_36_out, Reset, not_11_out);
  not not_11 (not_11_out, WP_q);
  D_Flip_Flop WP (.clk(Clock), .D(or_33_out), .Q(WP_q), .reset(Reset));  // open: Qn, preset, en
  not not_12 (not_12_out, insEn);
  Demultiplexer demultiplexer_8 (.out0(Ret_to_WR), .out1(ready2), .in(WR_q), .sel(WR_end));  // open: en
  Demultiplexer demultiplexer_9 (.out0(Ret_to_WP), .out1(ready3), .in(WP_q), .sel(WP_end));  // open: en
  Comparator #(.width(4), .mode("unsigned")) comparator_5 (.a(counter_5_q), .b(4'b0001), .eq(RI_end));  // open: gt, lt
  Demultiplexer demultiplexer_10 (.out0(Ret), .out1(\continue ), .in(insEn), .sel(RI_end));  // open: en
  Comparator #(.width(4), .mode("unsigned")) comparator_6 (.a(counter_6_q), .b(4'b0001), .eq(WR_end));  // open: gt, lt
  Comparator #(.width(4), .mode("unsigned")) comparator_7 (.a(counter_7_q), .b(4'b0001), .eq(WP_end));  // open: gt, lt

  // Other names for the same wires on the sheet: CLK = Clock; CLR = Reset; CS = Chip_Select;
  //   KBD_AVAIL = Kbd_Available; KBD_CLR = Kbd_Clear; KBD_DATA[6:0] = Kbd_ASCII_Data; RAM_A[15:0] = Address;
  //   RAM_INPUT_0[31:0] = RAM_In_0; RAM_INPUT_1[31:0] = RAM_In_1; RAM_INPUT_2[31:0] = RAM_In_2;
  //   RAM_INPUT_3[31:0] = RAM_In_3; RAM_MASK[3:0] = Mask; RAM_OUTPUT_0[31:0] = RAM_Out_0;
  //   RAM_OUTPUT_1[31:0] = RAM_Out_1; RAM_OUTPUT_2[31:0] = RAM_Out_2; RAM_OUTPUT_3[31:0] = RAM_Out_3;
  //   RD1[6:0] = TTY_ASCII_Data; TTY_DATA[6:0] = TTY_ASCII_Data; reading_lw = CS_Rlw; reading_pop = CS_Rpop;
  //   RW = nRead_Write; writing = CS_W

  // Notes on the sheet:
  //   KEYBOARD
  //   TTY
  //   SEQUENCING
  //   RAM ADDRESS
  //   DATA FROM RAM
  //   DATA TO RAM
  //   DATA WRITE MASK
  //   RAM TIMING
  //   RAM CONTROL
endmodule

module RAM_Dispatcher (
  input  [3:0] WriteTime,
  input  Clock,
  input  CLR,
  output [31:0] Data,
  output [15:0] Address,
  output [3:0] Mask,
  output Finished,
  output Write
);

  wire demultiplexer_2_out1, demultiplexer_3_out1, End, IDLE_q, IncAddr, Load, or_1_out, or_2_out, While_q,
       WriteEnd;
  wire [3:0] counter_1_q;
  wire [31:0] CurrentAddress_q;

  Counter #(.width(32), .max('hffffffff)) CurrentAddress (
    .count(IncAddr), .Q({CurrentAddress_q[31:18], Address, CurrentAddress_q[1:0]}), .clk(Clock), .clr(CLR));  // open: load, D, carry
  or or_1 (or_1_out, IncAddr, demultiplexer_3_out1, Finished);
  D_Flip_Flop IDLE (.clk(Clock), .D(or_1_out), .Q(IDLE_q), .preset(CLR));  // open: Qn, en, reset
  Demultiplexer #(.enable("false")) demultiplexer_1 (.out0(Load), .out1(Finished), .in(IDLE_q), .sel(End));
  D_Flip_Flop While (.clk(Clock), .D(or_2_out), .Q(While_q), .reset(CLR));  // open: Qn, preset, en
  or or_2 (or_2_out, Write, Load);
  RAM_part #(.addrWidth(18), .dataWidth(32)) ram_1 (
    .addr({Address, CurrentAddress_q[1:0]}), .data(Data), .clk(Clock));  // open: sel, ld, clr
  Demultiplexer #(.enable("false")) demultiplexer_2 (
    .out0(Write), .out1(demultiplexer_2_out1), .in(While_q), .sel(WriteEnd));
  Decoder_part #(.select(2)) decoder_1 (
    .out0(Mask[0]), .out1(Mask[1]), .out2(Mask[2]), .out3(Mask[3]), .sel(CurrentAddress_q[1:0]));  // open: en
  Demultiplexer #(.enable("false")) demultiplexer_3 (
    .out0(IncAddr), .out1(demultiplexer_3_out1), .in(demultiplexer_2_out1), .sel(End));
  Counter #(.width(4), .max('hf)) counter_1 (
    .load(Load), .D(WriteTime), .count(Write), .Q(counter_1_q), .clk(Clock));  // open: carry, clr
  Comparator #(.width(32)) comparator_1 (.a(Data), .b({32{1'b1}}), .eq(End));  // open: gt, lt
  Comparator #(.width(4)) comparator_2 (.a(4'b0000), .b(counter_1_q), .eq(WriteEnd));  // open: gt, lt

  // Other names for the same wires on the sheet: CLK = Clock; Count = Write; WT[3:0] = WriteTime
endmodule

module Complemento_A2 (
  input  [31:0] entrada,
  output [31:0] complemento,
  output carry
);

  wire [31:0] not_1_out;

  assign not_1_out = ~entrada;  // NOT_Gate not_1, 32 bits wide
  Adder #(.width(32)) adder_1 (.a(not_1_out), .b(32'h1), .out(complemento), .cout(carry));  // open: cin
endmodule

module Complemento_A2_64_bits (
  input  [31:0] in_1,
  input  [31:0] in_2,
  output [31:0] out_3,
  output [31:0] out_4
);

  wire complemento_a2_1_carry;
  wire [31:0] not_1_out;

  Complemento_A2 complemento_a2_1 (.entrada(in_1), .complemento(out_3), .carry(complemento_a2_1_carry));
  assign not_1_out = ~in_2;  // NOT_Gate not_1, 32 bits wide
  Adder #(.width(32)) adder_1 (.a({32{1'b0}}), .b(not_1_out), .out(out_4), .cin(complemento_a2_1_carry));  // open: cout
endmodule

module Multiplicador_con_signo (
  input  [31:0] Factor1,
  input  [31:0] Factor2,
  output [31:0] _31_0,
  output [31:0] _63_32
);

  wire or_1_out, or_2_out;
  wire [1:0] and_1_out;
  wire [1:1] and_2_out;
  wire [31:0] complemento_a2_1_complemento, complemento_a2_2_complemento, complemento_a2_64_bits_1_out_3,
       complemento_a2_64_bits_1_out_4, complemento_a2_64_bits_2_out_3, complemento_a2_64_bits_2_out_4,
       multiplier_1_cout, multiplier_1_out, multiplier_2_cout, multiplier_2_out, multiplier_3_cout,
       multiplier_3_out, multiplier_4_cout, multiplier_4_out, or_3_out, or_4_out;

  Complemento_A2 complemento_a2_1 (.entrada(Factor2), .complemento(complemento_a2_1_complemento));  // open: carry
  Complemento_A2 complemento_a2_2 (.entrada(Factor1), .complemento(complemento_a2_2_complemento));  // open: carry
  Multiplier #(.width(32)) multiplier_1 (
    .a(Factor1), .b(Factor2), .out(multiplier_1_out), .cout(multiplier_1_cout));  // open: cin
  Multiplier #(.width(32)) multiplier_2 (
    .a(Factor1), .b(complemento_a2_1_complemento), .out(multiplier_2_out), .cout(multiplier_2_cout));  // open: cin
  Multiplier #(.width(32)) multiplier_3 (
    .a(complemento_a2_2_complemento), .b(Factor2), .out(multiplier_3_out), .cout(multiplier_3_cout));  // open: cin
  or or_1 (or_1_out, Factor1[0], Factor1[1], Factor1[2], Factor1[3], Factor1[4], Factor1[5], Factor1[6], Factor1[7], Factor1[8], Factor1[9], Factor1[10], Factor1[11], Factor1[12], Factor1[13], Factor1[14], Factor1[15], Factor1[16], Factor1[17], Factor1[18], Factor1[19], Factor1[20], Factor1[21], Factor1[22], Factor1[23], Factor1[24], Factor1[25], Factor1[26], Factor1[27], Factor1[28], Factor1[29], Factor1[30], Factor1[31]);
  Complemento_A2_64_bits complemento_a2_64_bits_1 (
    .in_1(multiplier_2_out), .in_2(multiplier_2_cout), .out_3(complemento_a2_64_bits_1_out_3),
    .out_4(complemento_a2_64_bits_1_out_4));
  Complemento_A2_64_bits complemento_a2_64_bits_2 (
    .in_1(multiplier_3_out), .in_2(multiplier_3_cout), .out_3(complemento_a2_64_bits_2_out_3),
    .out_4(complemento_a2_64_bits_2_out_4));
  Multiplier #(.width(32)) multiplier_4 (
    .a(complemento_a2_2_complemento), .b(complemento_a2_1_complemento), .out(multiplier_4_out),
    .cout(multiplier_4_cout));  // open: cin
  or or_2 (or_2_out, Factor2[0], Factor2[1], Factor2[2], Factor2[3], Factor2[4], Factor2[5], Factor2[6], Factor2[7], Factor2[8], Factor2[9], Factor2[10], Factor2[11], Factor2[12], Factor2[13], Factor2[14], Factor2[15], Factor2[16], Factor2[17], Factor2[18], Factor2[19], Factor2[20], Factor2[21], Factor2[22], Factor2[23], Factor2[24], Factor2[25], Factor2[26], Factor2[27], Factor2[28], Factor2[29], Factor2[30], Factor2[31]);
  assign or_3_out = complemento_a2_64_bits_1_out_4 | 32'h80000000;  // OR_Gate or_3, 32 bits wide
  assign or_4_out = complemento_a2_64_bits_2_out_4 | 32'h80000000;  // OR_Gate or_4, 32 bits wide
  assign and_1_out = {Factor2[31], Factor1[31]} & {2{and_2_out[1]}};  // AND_Gate and_1, 2 bits wide
  and and_2 (and_2_out[1], or_1_out, or_2_out);
  Multiplexer #(.select(2), .width(32)) multiplexer_1 (
    .in0(multiplier_1_out), .in1(complemento_a2_64_bits_1_out_3), .in2(complemento_a2_64_bits_2_out_3),
    .in3(multiplier_4_out), .out(_31_0), .sel(and_1_out));  // open: en
  Multiplexer #(.select(2), .width(32)) multiplexer_2 (
    .in0(multiplier_1_cout), .in1(or_3_out), .in2(or_4_out), .in3(multiplier_4_cout), .out(_63_32),
    .sel(and_1_out));  // open: en
endmodule

module Division_con_signo (
  input  [31:0] Dividendo,
  input  [31:0] Divisor,
  output division_entre_0,
  output [31:0] cociente,
  output [31:0] resto
);

  wire or_1_out;
  wire [31:0] complemento_a2_1_complemento, complemento_a2_2_complemento, complemento_a2_3_complemento,
       complemento_a2_4_complemento, complemento_a2_5_complemento, complemento_a2_6_complemento,
       complemento_a2_7_complemento, complemento_a2_8_complemento, divider_1_out, divider_1_rem,
       divider_2_out, divider_2_rem, divider_3_out, divider_3_rem, divider_4_out, divider_4_rem;

  Divider #(.width(32)) divider_1 (
    .a(Dividendo), .b(Divisor), .out(divider_1_out), .rem(divider_1_rem));  // open: upper
  Complemento_A2 complemento_a2_1 (.entrada(Divisor), .complemento(complemento_a2_1_complemento));  // open: carry
  Complemento_A2 complemento_a2_2 (.entrada(Dividendo), .complemento(complemento_a2_2_complemento));  // open: carry
  Complemento_A2 complemento_a2_3 (.entrada(Dividendo), .complemento(complemento_a2_3_complemento));  // open: carry
  Complemento_A2 complemento_a2_4 (.entrada(Divisor), .complemento(complemento_a2_4_complemento));  // open: carry
  Divider #(.width(32)) divider_2 (
    .a(Dividendo), .b(complemento_a2_1_complemento), .out(divider_2_out), .rem(divider_2_rem));  // open: upper
  Complemento_A2 complemento_a2_5 (.entrada(divider_3_out), .complemento(complemento_a2_5_complemento));  // open: carry
  Divider #(.width(32)) divider_3 (
    .a(complemento_a2_2_complemento), .b(Divisor), .out(divider_3_out), .rem(divider_3_rem));  // open: upper
  Complemento_A2 complemento_a2_6 (.entrada(divider_3_rem), .complemento(complemento_a2_6_complemento));  // open: carry
  Divider #(.width(32)) divider_4 (
    .a(complemento_a2_3_complemento), .b(complemento_a2_4_complemento), .out(divider_4_out),
    .rem(divider_4_rem));  // open: upper
  Complemento_A2 complemento_a2_7 (.entrada(divider_2_out), .complemento(complemento_a2_7_complemento));  // open: carry
  Complemento_A2 complemento_a2_8 (.entrada(divider_4_rem), .complemento(complemento_a2_8_complemento));  // open: carry
  or or_1 (or_1_out, Divisor[0], Divisor[1], Divisor[2], Divisor[3], Divisor[4], Divisor[5], Divisor[6], Divisor[7], Divisor[8], Divisor[9], Divisor[10], Divisor[11], Divisor[12], Divisor[13], Divisor[14], Divisor[15], Divisor[16], Divisor[17], Divisor[18], Divisor[19], Divisor[20], Divisor[21], Divisor[22], Divisor[23], Divisor[24], Divisor[25], Divisor[26], Divisor[27], Divisor[28], Divisor[29], Divisor[30], Divisor[31]);
  Multiplexer #(.select(2), .width(32)) multiplexer_1 (
    .in0(divider_1_out), .in1(complemento_a2_7_complemento), .in2(complemento_a2_5_complemento),
    .in3(divider_4_out), .out(cociente), .sel({Dividendo[31], Divisor[31]}));  // open: en
  Multiplexer #(.select(2), .width(32)) multiplexer_2 (
    .in0(divider_1_rem), .in1(divider_2_rem), .in2(complemento_a2_6_complemento),
    .in3(complemento_a2_8_complemento), .out(resto), .sel({Dividendo[31], Divisor[31]}));  // open: en
  not not_1 (division_entre_0, or_1_out);
endmodule

module ALU (
  input  [31:0] A,
  input  [31:0] B,
  input  [2:0] ALUOP,
  input  Clock,
  input  Reset,
  input  mult,
  input  mulu,
  input  div,
  input  divu,
  input  ready,
  output [31:0] HI,
  output [31:0] ALU_Result,
  output [31:0] LO
);

  wire and_2_out, and_3_out, comparator_1_lt, comparator_2_lt, HI___LO, or_2_out, or_3_out;
  wire [31:0] A_B, A_B_t, A_B_t_t, A_B_t_t_t, A_B_t_t_t_t, A_B_t_t_t_t_t, A_B_t_t_t_t_t_t, A_B_t_t_t_t_t_t_t,
       AnorB, mul31_0, mul63_32, multiplexer_2_out, multiplexer_3_out, multiplexer_4_out, multiplexer_5_out,
       multiplexer_6_out, multiplexer_7_out, mulu31_0, mulu63_32, us_A_B, us_A_B_t, us_A_B_t_t;

  Adder #(.width(32)) adder_1 (.a(A), .b(B), .out(A_B_t_t));  // open: cin, cout
  Subtractor #(.width(32)) subtractor_1 (.a(A), .b(B), .out(A_B_t_t_t));  // open: bin, bout
  Multiplicador_con_signo multiplicador_con_signo_1 (.Factor1(A), .Factor2(B), ._31_0(mul31_0), ._63_32(mul63_32));
  Division_con_signo division_con_signo_1 (
    .Dividendo(A), .Divisor(B), .cociente(A_B_t_t_t_t), .resto(A_B));  // open: division_entre_0
  Divider #(.width(32)) divider_1 (.a(A), .b(B), .out(us_A_B_t), .rem(us_A_B));  // open: upper
  Multiplexer #(.select(3), .width(32)) multiplexer_1 (
    .in0(A_B_t_t), .in1(A_B_t_t_t), .in2(A_B_t), .in3(A_B_t_t_t_t_t_t_t), .in4(A_B_t_t_t_t_t_t),
    .in5(A_B_t_t_t_t_t), .in6(us_A_B_t_t), .in7(AnorB), .out(ALU_Result), .sel(ALUOP));  // open: en
  Multiplier #(.width(32)) multiplier_1 (.a(A), .b(B), .out(mulu31_0), .cout(mulu63_32));  // open: cin
  assign A_B_t = A & B;  // AND_Gate and_1, 32 bits wide
  assign A_B_t_t_t_t_t_t_t = A | B;  // OR_Gate or_1, 32 bits wide
  assign A_B_t_t_t_t_t_t = A ^ B;  // XOR_Gate xor_1, 32 bits wide
  Comparator #(.width(32)) comparator_1 (.a(A), .b(B), .lt(comparator_1_lt));  // open: gt, eq
  Comparator #(.width(32), .mode("unsigned")) comparator_2 (.a(A), .b(B), .lt(comparator_2_lt));  // open: gt, eq
  assign AnorB = ~(A | B);  // NOR_Gate nor_1, 32 bits wide
  Multiplexer #(.width(32)) multiplexer_2 (
    .in0(mul63_32), .in1(mulu63_32), .out(multiplexer_2_out), .sel(mulu));  // open: en
  Multiplexer #(.width(32)) multiplexer_3 (.in0(A_B), .in1(us_A_B), .out(multiplexer_3_out), .sel(divu));  // open: en
  Multiplexer #(.width(32)) multiplexer_4 (
    .in0(mul31_0), .in1(mulu31_0), .out(multiplexer_4_out), .sel(mulu));  // open: en
  Multiplexer #(.width(32)) multiplexer_5 (
    .in0(A_B_t_t_t_t), .in1(us_A_B_t), .out(multiplexer_5_out), .sel(divu));  // open: en
  assign A_B_t_t_t_t_t = {{31{1'b0}}, comparator_1_lt};  // Bit_Extender bit_extender_1
  assign us_A_B_t_t = {{31{1'b0}}, comparator_2_lt};  // Bit_Extender bit_extender_2
  Multiplexer #(.width(32)) multiplexer_6 (
    .in0(multiplexer_2_out), .in1(multiplexer_3_out), .out(multiplexer_6_out), .sel(or_2_out));  // open: en
  or or_2 (or_2_out, divu, div);
  Multiplexer #(.width(32)) multiplexer_7 (
    .in0(multiplexer_4_out), .in1(multiplexer_5_out), .out(multiplexer_7_out), .sel(or_3_out));  // open: en
  or or_3 (or_3_out, divu, div);
  or or_4 (HI___LO, mult, mulu, div, divu);
  and and_2 (and_2_out, ready, HI___LO);
  and and_3 (and_3_out, ready, HI___LO);
  Register #(.width(32)) u_HI (.D(multiplexer_6_out), .en(and_2_out), .Q(HI), .clk(Clock), .clr(Reset));
  Register #(.width(32)) u_LO (.D(multiplexer_7_out), .en(and_3_out), .Q(LO), .clk(Clock), .clr(Reset));

  // Other names for the same wires on the sheet: CLK = Clock; OP[2:0] = ALUOP; RST = Reset
endmodule

module Register_File (
  input  [31:0] WD3,
  input  Update_Push,
  input  upop,
  input  clock,
  input  Reset,
  input  WE3,
  input  ready,
  input  [4:0] A3,
  input  [4:0] A1,
  input  [4:0] A2,
  output [31:0] SP,
  output [31:0] RD1,
  output [31:0] RD2
);

  wire and_3_out, L0, L1, L2, L3, L4, L5, L6, L7, L8, L9, L10, L11, L12, L13, L14, L15, L16, L17, L18, L19,
       L20, L21, L22, L23, L24, L25, L26, L27, L28, L29, L30, L31, or_1_out;
  wire [4:0] and_1_out, bit_extender_1_out;
  wire [31:0] adder_1_out, and_2_out, multiplexer_3_out, multiplexer_4_out, Q0, Q1, Q2, Q3, Q4, Q5, Q6, Q7,
       Q8, Q9, Q10, Q11, Q12, Q13, Q14, Q15, Q16, Q17, Q18, Q19, Q20, Q21, Q22, Q23, Q24, Q25, Q26, Q27, Q28,
       Q29, Q30, sp_t, subtractor_1_out, subtractor_2_out;

  Decoder_part #(.select(5)) decoder_1 (
    .out0(L0), .out1(L1), .out2(L2), .out3(L3), .out4(L4), .out5(L5), .out6(L6), .out7(L7), .out8(L8),
    .out9(L9), .out10(L10), .out11(L11), .out12(L12), .out13(L13), .out14(L14), .out15(L15), .out16(L16),
    .out17(L17), .out18(L18), .out19(L19), .out20(L20), .out21(L21), .out22(L22), .out23(L23), .out24(L24),
    .out25(L25), .out26(L26), .out27(L27), .out28(L28), .out29(L29), .out30(L30), .out31(L31), .sel(and_1_out));  // open: en
  assign and_1_out = A3 & bit_extender_1_out;  // AND_Gate and_1, 5 bits wide
  assign and_2_out = WD3 & {32{1'b0}};  // AND_Gate and_2, 32 bits wide
  Register #(.width(32)) R0 (.D(and_2_out), .en(L0), .Q(Q0), .clk(clock), .clr(Reset));
  Register #(.width(32)) R1 (.D(WD3), .en(L1), .Q(Q1), .clk(clock), .clr(Reset));
  Register #(.width(32)) R2 (.D(WD3), .en(L2), .Q(Q2), .clk(clock), .clr(Reset));
  Register #(.width(32)) R3 (.D(WD3), .en(L3), .Q(Q3), .clk(clock), .clr(Reset));
  assign bit_extender_1_out = {{4{and_3_out}}, and_3_out};  // Bit_Extender bit_extender_1
  and and_3 (and_3_out, WE3, ready);
  Register #(.width(32)) R4 (.D(WD3), .en(L4), .Q(Q4), .clk(clock), .clr(Reset));
  Register #(.width(32)) R5 (.D(WD3), .en(L5), .Q(Q5), .clk(clock), .clr(Reset));
  Register #(.width(32)) R6 (.D(WD3), .en(L6), .Q(Q6), .clk(clock), .clr(Reset));
  Register #(.width(32)) R7 (.D(WD3), .en(L7), .Q(Q7), .clk(clock), .clr(Reset));
  Register #(.width(32)) R8 (.D(WD3), .en(L8), .Q(Q8), .clk(clock), .clr(Reset));
  Register #(.width(32)) R9 (.D(WD3), .en(L9), .Q(Q9), .clk(clock), .clr(Reset));
  Register #(.width(32)) R10 (.D(WD3), .en(L10), .Q(Q10), .clk(clock), .clr(Reset));
  Register #(.width(32)) R11 (.D(WD3), .en(L11), .Q(Q11), .clk(clock), .clr(Reset));
  Register #(.width(32)) R12 (.D(WD3), .en(L12), .Q(Q12), .clk(clock), .clr(Reset));
  Register #(.width(32)) R13 (.D(WD3), .en(L13), .Q(Q13), .clk(clock), .clr(Reset));
  Register #(.width(32)) R14 (.D(WD3), .en(L14), .Q(Q14), .clk(clock), .clr(Reset));
  Register #(.width(32)) R15 (.D(WD3), .en(L15), .Q(Q15), .clk(clock), .clr(Reset));
  Multiplexer #(.select(5), .width(32)) multiplexer_1 (
    .in0(Q0), .in1(Q1), .in2(Q2), .in3(Q3), .in4(Q4), .in5(Q5), .in6(Q6), .in7(Q7), .in8(Q8), .in9(Q9),
    .in10(Q10), .in11(Q11), .in12(Q12), .in13(Q13), .in14(Q14), .in15(Q15), .in16(Q16), .in17(Q17),
    .in18(Q18), .in19(Q19), .in20(Q20), .in21(Q21), .in22(Q22), .in23(Q23), .in24(Q24), .in25(Q25),
    .in26(Q26), .in27(Q27), .in28(Q28), .in29(Q29), .in30(Q30), .in31(SP), .out(RD1), .sel(A1));  // open: en
  Register #(.width(32)) R16 (.D(WD3), .en(L16), .Q(Q16), .clk(clock), .clr(Reset));
  Register #(.width(32)) R17 (.D(WD3), .en(L17), .Q(Q17), .clk(clock), .clr(Reset));
  Register #(.width(32)) R18 (.D(WD3), .en(L18), .Q(Q18), .clk(clock), .clr(Reset));
  Register #(.width(32)) R19 (.D(WD3), .en(L19), .Q(Q19), .clk(clock), .clr(Reset));
  Register #(.width(32)) R20 (.D(WD3), .en(L20), .Q(Q20), .clk(clock), .clr(Reset));
  Register #(.width(32)) R21 (.D(WD3), .en(L21), .Q(Q21), .clk(clock), .clr(Reset));
  Register #(.width(32)) R22 (.D(WD3), .en(L22), .Q(Q22), .clk(clock), .clr(Reset));
  Register #(.width(32)) R23 (.D(WD3), .en(L23), .Q(Q23), .clk(clock), .clr(Reset));
  Register #(.width(32)) R24 (.D(WD3), .en(L24), .Q(Q24), .clk(clock), .clr(Reset));
  Register #(.width(32)) R25 (.D(WD3), .en(L25), .Q(Q25), .clk(clock), .clr(Reset));
  Register #(.width(32)) R26 (.D(WD3), .en(L26), .Q(Q26), .clk(clock), .clr(Reset));
  Register #(.width(32)) R27 (.D(WD3), .en(L27), .Q(Q27), .clk(clock), .clr(Reset));
  Register #(.width(32)) R28 (.D(WD3), .en(L28), .Q(Q28), .clk(clock), .clr(Reset));
  Register #(.width(32)) R29 (.D(WD3), .en(L29), .Q(Q29), .clk(clock), .clr(Reset));
  Register #(.width(32)) R30 (.D(WD3), .en(L30), .Q(Q30), .clk(clock), .clr(Reset));
  Subtractor #(.width(32)) subtractor_1 (.a(32'hffffc), .b(WD3), .out(subtractor_1_out));  // open: bin, bout
  Adder #(.width(32)) adder_1 (.a(sp_t), .b(32'h4), .out(adder_1_out));  // open: cin, cout
  Subtractor #(.width(32)) subtractor_2 (.a(sp_t), .b(32'h4), .out(subtractor_2_out));  // open: bin, bout
  Multiplexer #(.select(5), .width(32)) multiplexer_2 (
    .in0(Q0), .in1(Q1), .in2(Q2), .in3(Q3), .in4(Q4), .in5(Q5), .in6(Q6), .in7(Q7), .in8(Q8), .in9(Q9),
    .in10(Q10), .in11(Q11), .in12(Q12), .in13(Q13), .in14(Q14), .in15(Q15), .in16(Q16), .in17(Q17),
    .in18(Q18), .in19(Q19), .in20(Q20), .in21(Q21), .in22(Q22), .in23(Q23), .in24(Q24), .in25(Q25),
    .in26(Q26), .in27(Q27), .in28(Q28), .in29(Q29), .in30(Q30), .in31(SP), .out(RD2), .sel(A2));  // open: en
  Multiplexer #(.width(32)) multiplexer_3 (
    .in0(subtractor_1_out), .in1(adder_1_out), .out(multiplexer_3_out), .sel(Update_Push));  // open: en
  Multiplexer #(.width(32)) multiplexer_4 (
    .in0(multiplexer_3_out), .in1(subtractor_2_out), .out(multiplexer_4_out), .sel(upop));  // open: en
  or or_1 (or_1_out, Update_Push, upop, L31);
  Register #(.width(32)) R31 (.D(multiplexer_4_out), .en(or_1_out), .Q(sp_t), .clk(clock), .clr(Reset));
  Subtractor #(.width(32)) subtractor_3 (.a(32'hffffc), .b(sp_t), .out(SP));  // open: bin, bout

  // Other names for the same wires on the sheet: DI[31:0] = WD3; Q31[31:0] = SP; RST = Reset; upsush = Update_Push
endmodule

module Chronometer (
  input  RESET,
  input  Count,
  input  CLOCK,
  input  [3:0] Read_Time,
  output CHIP_SELECT,
  output READY
);

  wire C, demultiplexer_1_out0, demultiplexer_1_out1, F, IDLE_q, or_1_out, or_2_out, or_3_out;
  wire [3:0] pr;

  or or_1 (or_1_out, demultiplexer_1_out0, F);
  Counter #(.width(4), .max('hf)) counter_1 (.Q(pr), .clk(CLOCK), .clr(or_2_out));  // open: load, D, count, carry
  or or_2 (or_2_out, RESET, IDLE_q);
  D_Flip_Flop IDLE (.clk(CLOCK), .D(or_1_out), .Q(IDLE_q), .preset(RESET));  // open: Qn, en, reset
  Demultiplexer demultiplexer_1 (
    .out0(demultiplexer_1_out0), .out1(demultiplexer_1_out1), .in(IDLE_q), .sel(Count));  // open: en
  or or_3 (or_3_out, demultiplexer_1_out1, C);
  Comparator #(.width(4), .mode("unsigned")) comparator_1 (.a(pr), .b(Read_Time), .eq(READY));  // open: gt, lt
  D_Flip_Flop COUNTING (.clk(CLOCK), .D(or_3_out), .Q(CHIP_SELECT), .reset(RESET));  // open: Qn, preset, en
  Demultiplexer demultiplexer_2 (.out0(C), .out1(F), .in(CHIP_SELECT), .sel(READY));  // open: en

  // Other names for the same wires on the sheet: CLK = CLOCK; CS = CHIP_SELECT; End = READY; RST = RESET;
  //   Time[3:0] = Read_Time
endmodule

module Memory_Reader (
  input  [31:0] Current_Address,
  input  [31:0] RAM_OUT_0,
  input  [31:0] RAM_OUT_1,
  input  [31:0] RAM_OUT_2,
  input  [31:0] RAM_OUT_3,
  output [15:0] Address,
  output [31:0] Instruction
);

  Multiplexer #(.select(2), .width(32)) multiplexer_1 (
    .in0(RAM_OUT_0), .in1(RAM_OUT_1), .in2(RAM_OUT_2), .in3(RAM_OUT_3),
    .out({Instruction[7:0], Instruction[15:8], Instruction[23:16], Instruction[31:24]}),
    .sel(Current_Address[3:2]));  // open: en

  assign Address = Current_Address[19:4];

  // Other names for the same wires on the sheet: offSet[1:0] = Current_Address[3:2]
endmodule

module Program_Counter (
  input  Clock,
  input  Reset,
  input  PC_ENABLE,
  input  [31:0] Next_Address,
  output [31:0] Current_Address
);

  Register #(.width(32)) Program_Counter (
    .D(Next_Address), .en(PC_ENABLE), .Q(Current_Address), .clk(Clock), .clr(Reset));

  // Other names for the same wires on the sheet: CLK = Clock; RST = Reset
endmodule

module Decoder (
  input  [31:0] in_1,
  output [4:0] RT,
  output [25:0] Destiny_Jump,
  output [4:0] RD,
  output [4:0] RS,
  output [15:0] Const,
  output lw,
  output sw,
  output mult,
  output div,
  output add,
  output sub,
  output mulu,
  output jr,
  output pop,
  output tty,
  output rnd,
  output nop,
  output push,
  output divu,
  output mfhi,
  output halt,
  output kbd,
  output slt,
  output mflo,
  output \or ,
  output \nor ,
  output \xor ,
  output \and ,
  output sltu,
  output xori,
  output ori,
  output andi,
  output addi,
  output beq,
  output slti,
  output bne,
  output bltz,
  output j,
  output blez,
  output bgtz,
  output sltiu,
  output WE3,
  output [2:0] ALU_OP
);

  wire _00_enable, A_B, and_t, nor_2_out, or_6_out, or_7_out, or_8_out, or_t, special_enable, stack_enable,
       us_A_B, word_enable, xor_t;
  wire [2:0] multiplexer_1_out, multiplexer_2_out, multiplexer_3_out, multiplexer_4_out, multiplexer_5_out,
       multiplexer_6_out;

  or or_1 (xor_t, xori, \xor );
  or or_2 (and_t, \and , andi);
  nor nor_1 (_00_enable, in_1[31], in_1[30], in_1[29], in_1[28], in_1[27], in_1[26]);
  or or_3 (or_t, \or , ori);
  Operations00 operations00_1 (
    .FuncCode(in_1[5:0]), .enable(_00_enable), .mult(mult), .div(div), .add(add), .sub(sub), .\nor (\nor ),
    .\xor (\xor ), .\and (\and ), .\or (\or ), .mfhi(mfhi), .mflo(mflo), .slt(slt), .sltu(sltu), .nop(nop),
    .jr(jr), .mulu(mulu), .divu(divu));
  or or_4 (A_B, slt, slti);
  or or_5 (us_A_B, sltiu, sltu);
  Multiplexer #(.width(3)) multiplexer_1 (.in0(3'b000), .in1(3'b001), .out(multiplexer_1_out), .sel(sub));  // open: en
  Multiplexer #(.width(3)) multiplexer_2 (.in0(3'b010), .in1(3'b011), .out(multiplexer_2_out), .sel(or_t));  // open: en
  Multiplexer #(.width(3)) multiplexer_3 (.in0(3'b100), .in1(3'b101), .out(multiplexer_3_out), .sel(A_B));  // open: en
  Multiplexer #(.width(3)) multiplexer_4 (
    .in0(3'b110), .in1(3'b111), .out(multiplexer_4_out), .sel(\nor ));  // open: en
  and and_1 (word_enable, in_1[31], ~in_1[30]);  // AND_Gate
  Multiplexer #(.width(3)) multiplexer_5 (
    .in0(multiplexer_1_out), .in1(multiplexer_2_out), .out(multiplexer_5_out), .sel(or_6_out));  // open: en
  or or_6 (or_6_out, and_t, or_t);
  Multiplexer #(.width(3)) multiplexer_6 (
    .in0(multiplexer_3_out), .in1(multiplexer_4_out), .out(multiplexer_6_out), .sel(or_7_out));  // open: en
  or or_7 (or_7_out, us_A_B, \nor );
  OperationsWord operationsword_1 (.enable(word_enable), .OpCode(in_1[31:26]), .lw(lw), .sw(sw));
  nor nor_2 (nor_2_out, _00_enable, word_enable, special_enable, stack_enable);
  Multiplexer #(.width(3)) multiplexer_7 (
    .in0(multiplexer_5_out), .in1(multiplexer_6_out), .out(ALU_OP), .sel(or_8_out));  // open: en
  or or_8 (or_8_out, us_A_B, \nor , A_B, xor_t);
  and and_2 (special_enable, in_1[31], in_1[30], in_1[29], in_1[28], in_1[27], in_1[26]);
  OperationsI operationsi_1 (
    .enable(nor_2_out), .OpCode(in_1[31:26]), .ori(ori), .xori(xori), .addi(addi), .andi(andi), .beq(beq),
    .bne(bne), .slti(slti), .sltiu(sltiu), .bltz(bltz), .j(j), .blez(blez), .bgtz(bgtz));
  OperationsSpecial operationsspecial_1 (
    .enable(special_enable), .FuncCode(in_1[5:0]), .rnd(rnd), .kbd(kbd), .halt(halt), .tty(tty));
  and and_3 (stack_enable, in_1[31], in_1[30], in_1[29], ~in_1[28], ~in_1[27], ~in_1[26]);  // AND_Gate
  OperationsStack operationsstack_1 (.enable(stack_enable), .FuncCode(in_1[5:0]), .pop(pop), .push(push));
  or or_9 (WE3, mfhi, mflo, us_A_B, add, sub, addi, and_t, or_t, \nor , xor_t, A_B);

  assign Const = in_1[15:0];
  assign Destiny_Jump = in_1[25:0];
  assign RD = in_1[15:11];
  assign RS = in_1[25:21];
  assign RT = in_1[20:16];

  // Other names for the same wires on the sheet: and0 = \and ; FuncCode[5:0] = in_1[5:0]; Instruction[31:0] = in_1;
  //   OpCode[5:0] = in_1[31:26]; or0 = \or ; xor0 = \xor 
endmodule

module Operations00 (
  input  [5:0] FuncCode,
  input  enable,
  output mult,
  output div,
  output add,
  output sub,
  output \nor ,
  output \xor ,
  output \and ,
  output \or ,
  output mfhi,
  output mflo,
  output slt,
  output sltu,
  output nop,
  output jr,
  output mulu,
  output divu
);

  wire and_1_out, and_2_out, and_3_out, and_5_out, and_9_out, and_10_out, and_11_out, and_12_out, and_17_out,
       and_19_out, and_21_out, and_23_out, and_25_out, and_26_out, and_27_out, and_28_out;

  and and_1 (and_1_out, ~FuncCode[0], ~FuncCode[1], ~FuncCode[2], ~FuncCode[3], ~FuncCode[4], FuncCode[5]);  // AND_Gate
  and and_2 (and_2_out, ~FuncCode[0], ~FuncCode[1], FuncCode[2], ~FuncCode[3], ~FuncCode[4], FuncCode[5]);  // AND_Gate
  and and_3 (and_3_out, ~FuncCode[0], FuncCode[1], ~FuncCode[2], FuncCode[3], ~FuncCode[4], FuncCode[5]);  // AND_Gate
  and and_4 (slt, and_3_out, enable);
  and and_5 (and_5_out, ~FuncCode[0], ~FuncCode[1], ~FuncCode[2], ~FuncCode[3], ~FuncCode[4], ~FuncCode[5]);  // AND_Gate
  and and_6 (nop, and_5_out, enable);
  and and_7 (add, and_1_out, enable);
  and and_8 (\and , and_2_out, enable);
  and and_9 (and_9_out, ~FuncCode[0], FuncCode[1], ~FuncCode[2], ~FuncCode[3], ~FuncCode[4], FuncCode[5]);  // AND_Gate
  and and_10 (and_10_out, FuncCode[0], ~FuncCode[1], FuncCode[2], ~FuncCode[3], ~FuncCode[4], FuncCode[5]);  // AND_Gate
  and and_11 (and_11_out, FuncCode[0], FuncCode[1], ~FuncCode[2], FuncCode[3], ~FuncCode[4], FuncCode[5]);  // AND_Gate
  and and_12 (and_12_out, ~FuncCode[0], ~FuncCode[1], ~FuncCode[2], FuncCode[3], ~FuncCode[4], ~FuncCode[5]);  // AND_Gate
  and and_13 (sub, and_9_out, enable);
  and and_14 (\or , and_10_out, enable);
  and and_15 (sltu, and_11_out, enable);
  and and_16 (jr, and_12_out, enable);
  and and_17 (and_17_out, ~FuncCode[0], ~FuncCode[1], ~FuncCode[2], FuncCode[3], FuncCode[4], ~FuncCode[5]);  // AND_Gate
  and and_18 (mult, and_17_out, enable);
  and and_19 (and_19_out, FuncCode[0], FuncCode[1], FuncCode[2], ~FuncCode[3], ~FuncCode[4], FuncCode[5]);  // AND_Gate
  and and_20 (\nor , and_19_out, enable);
  and and_21 (and_21_out, ~FuncCode[0], ~FuncCode[1], ~FuncCode[2], ~FuncCode[3], FuncCode[4], ~FuncCode[5]);  // AND_Gate
  and and_22 (mfhi, and_21_out, enable);
  and and_23 (and_23_out, FuncCode[0], ~FuncCode[1], ~FuncCode[2], FuncCode[3], FuncCode[4], ~FuncCode[5]);  // AND_Gate
  and and_24 (mulu, and_23_out, enable);
  and and_25 (and_25_out, ~FuncCode[0], FuncCode[1], ~FuncCode[2], FuncCode[3], FuncCode[4], ~FuncCode[5]);  // AND_Gate
  and and_26 (and_26_out, ~FuncCode[0], ~FuncCode[1], ~FuncCode[2], FuncCode[3], ~FuncCode[4], FuncCode[5]);  // AND_Gate
  and and_27 (and_27_out, ~FuncCode[0], FuncCode[1], ~FuncCode[2], ~FuncCode[3], FuncCode[4], ~FuncCode[5]);  // AND_Gate
  and and_28 (and_28_out, FuncCode[0], FuncCode[1], ~FuncCode[2], FuncCode[3], FuncCode[4], ~FuncCode[5]);  // AND_Gate
  and and_29 (div, and_25_out, enable);
  and and_30 (\xor , and_26_out, enable);
  and and_31 (mflo, and_27_out, enable);
  and and_32 (divu, and_28_out, enable);

  // Other names for the same wires on the sheet: en = enable; _0 = FuncCode[0]; _1 = FuncCode[1]; _2 = FuncCode[2];
  //   _3 = FuncCode[3]; _4 = FuncCode[4]; _5 = FuncCode[5]
endmodule

module OperationsI (
  input  enable,
  input  [5:0] OpCode,
  output ori,
  output xori,
  output addi,
  output andi,
  output beq,
  output bne,
  output slti,
  output sltiu,
  output bltz,
  output j,
  output blez,
  output bgtz
);

  wire and_1_out, and_2_out, and_3_out, and_7_out, and_8_out, and_9_out, and_13_out, and_14_out, and_15_out,
       and_19_out, and_20_out, and_21_out;

  and and_1 (and_1_out, ~OpCode[0], ~OpCode[1], ~OpCode[2], OpCode[3]);  // AND_Gate
  and and_2 (and_2_out, ~OpCode[0], OpCode[1], ~OpCode[2], OpCode[3]);  // AND_Gate
  and and_3 (and_3_out, ~OpCode[0], OpCode[1], OpCode[2], ~OpCode[3]);  // AND_Gate
  and and_4 (addi, and_1_out, enable);
  and and_5 (slti, and_2_out, enable);
  and and_6 (blez, and_3_out, enable);
  and and_7 (and_7_out, ~OpCode[0], ~OpCode[1], OpCode[2], OpCode[3]);  // AND_Gate
  and and_8 (and_8_out, OpCode[0], OpCode[1], ~OpCode[2], OpCode[3]);  // AND_Gate
  and and_9 (and_9_out, OpCode[0], OpCode[1], OpCode[2], ~OpCode[3]);  // AND_Gate
  and and_10 (andi, and_7_out, enable);
  and and_11 (sltiu, and_8_out, enable);
  and and_12 (bgtz, and_9_out, enable);
  and and_13 (and_13_out, OpCode[0], ~OpCode[1], OpCode[2], OpCode[3]);  // AND_Gate
  and and_14 (and_14_out, ~OpCode[0], ~OpCode[1], OpCode[2], ~OpCode[3]);  // AND_Gate
  and and_15 (and_15_out, OpCode[0], ~OpCode[1], ~OpCode[2], ~OpCode[3]);  // AND_Gate
  and and_16 (ori, and_13_out, enable);
  and and_17 (beq, and_14_out, enable);
  and and_18 (bltz, and_15_out, enable);
  and and_19 (and_19_out, ~OpCode[0], OpCode[1], OpCode[2], OpCode[3]);  // AND_Gate
  and and_20 (and_20_out, OpCode[0], ~OpCode[1], OpCode[2], ~OpCode[3]);  // AND_Gate
  and and_21 (and_21_out, ~OpCode[0], OpCode[1], ~OpCode[2], ~OpCode[3]);  // AND_Gate
  and and_22 (xori, and_19_out, enable);
  and and_23 (bne, and_20_out, enable);
  and and_24 (j, and_21_out, enable);

  // Other names for the same wires on the sheet: en = enable; _0 = OpCode[0]; _1 = OpCode[1]; _2 = OpCode[2];
  //   _3 = OpCode[3]; _4 = OpCode[4]; _5 = OpCode[5]
endmodule

module OperationsWord (
  input  enable,
  input  [5:0] OpCode,
  output lw,
  output sw
);

  wire decoder_1_out0, decoder_1_out1;

  Decoder_part decoder_1 (.out0(decoder_1_out0), .out1(decoder_1_out1), .sel(OpCode[3]));  // open: en
  and and_1 (lw, decoder_1_out0, enable);
  and and_2 (sw, decoder_1_out1, enable);

  // Other names for the same wires on the sheet: en = enable
endmodule

module OperationsStack (
  input  enable,
  input  [5:0] FuncCode,
  output pop,
  output push
);

  wire decoder_1_out0, decoder_1_out1;

  Decoder_part decoder_1 (.out0(decoder_1_out0), .out1(decoder_1_out1), .sel(FuncCode[0]));  // open: en
  and and_1 (pop, decoder_1_out0, enable);
  and and_2 (push, decoder_1_out1, enable);

  // Other names for the same wires on the sheet: en = enable
endmodule

module OperationsSpecial (
  input  enable,
  input  [5:0] FuncCode,
  output rnd,
  output kbd,
  output halt,
  output tty
);

  wire and_1_out, and_3_out, and_5_out, and_7_out;

  and and_1 (and_1_out, FuncCode[0], FuncCode[1], FuncCode[2], FuncCode[3], FuncCode[4], FuncCode[5]);
  and and_2 (halt, and_1_out, enable);
  and and_3 (and_3_out, FuncCode[0], ~FuncCode[1], ~FuncCode[2], ~FuncCode[3], ~FuncCode[4], ~FuncCode[5]);  // AND_Gate
  and and_4 (tty, and_3_out, enable);
  and and_5 (and_5_out, ~FuncCode[0], FuncCode[1], ~FuncCode[2], ~FuncCode[3], ~FuncCode[4], ~FuncCode[5]);  // AND_Gate
  and and_6 (rnd, and_5_out, enable);
  and and_7 (and_7_out, ~FuncCode[0], ~FuncCode[1], FuncCode[2], ~FuncCode[3], ~FuncCode[4], ~FuncCode[5]);  // AND_Gate
  and and_8 (kbd, and_7_out, enable);

  // Other names for the same wires on the sheet: en = enable; _0 = FuncCode[0]; _1 = FuncCode[1]; _2 = FuncCode[2];
  //   _3 = FuncCode[3]; _4 = FuncCode[4]; _5 = FuncCode[5]
endmodule

module BitExtenderBranch (
  input  [15:0] Const,
  output [31:0] out_2
);


  assign out_2 = {{15{Const[15]}}, Const[14:0], 2'b00};
endmodule

module BitExtenderJump (
  input  [25:0] DestinyJump,
  input  [31:0] PC,
  output [31:0] ExtendedBit
);


  assign ExtendedBit = {PC[31:28], DestinyJump, 2'b00};
endmodule

module Branch_Control (
  input  [31:0] RS,
  input  [31:0] RT,
  input  [31:0] Current_Address,
  input  [15:0] Const,
  input  [25:0] DestinyJump,
  input  beq,
  input  bne,
  input  blez,
  input  bgtz,
  input  bltz,
  input  j,
  input  jr,
  output [31:0] New_Address
);

  wire and_1_out, and_2_out, and_3_out, and_4_out, and_5_out, branch_t, comparator_2_eq, eq, gtz, lez, ltz,
       neq, or_2_out;
  wire [31:0] Branch, Extended_Bit, Jump_Address, multiplexer_1_out, multiplexer_2_out, PC___4;

  Adder #(.width(32)) adder_1 (.a(PC___4), .b(Extended_Bit), .out(Branch));  // open: cin, cout
  Adder #(.width(32)) adder_2 (.a(Current_Address), .b(32'h4), .out(PC___4));  // open: cin, cout
  BitExtenderBranch bitextenderbranch_1 (.Const(Const), .out_2(Extended_Bit));
  BitExtenderJump bitextenderjump_1 (.DestinyJump(DestinyJump), .PC(Current_Address), .ExtendedBit(Jump_Address));
  Comparator #(.width(32), .mode("unsigned")) comparator_1 (.a(RS), .b(RT), .eq(eq));  // open: gt, lt
  and and_1 (and_1_out, beq, eq);
  Multiplexer #(.width(32)) multiplexer_1 (
    .in0(PC___4), .in1(Branch), .out(multiplexer_1_out), .sel(branch_t));  // open: en
  Multiplexer #(.width(32)) multiplexer_2 (
    .in0(Jump_Address), .in1(RS), .out(multiplexer_2_out), .sel(jr));  // open: en
  and and_2 (and_2_out, bne, neq);
  not not_1 (neq, eq);
  or or_1 (branch_t, and_1_out, and_2_out, and_3_out, and_4_out, and_5_out);
  and and_3 (and_3_out, blez, lez);
  or or_2 (or_2_out, jr, j);
  and and_4 (and_4_out, bgtz, gtz);
  Multiplexer #(.width(32)) multiplexer_3 (
    .in0(multiplexer_1_out), .in1(multiplexer_2_out), .out(New_Address), .sel(or_2_out));  // open: en
  and and_5 (and_5_out, bltz, ltz);
  Comparator #(.width(32)) comparator_2 (.a(RS), .b({32{1'b0}}), .gt(gtz), .eq(comparator_2_eq), .lt(ltz));
  or or_3 (lez, comparator_2_eq, ltz);

  // Other names for the same wires on the sheet: PC[31:0] = Current_Address
endmodule

module Memory_Writer (
  input  [31:0] Data_In,
  input  [31:0] Address_In,
  output [31:0] Data_In_0,
  output [31:0] Data_In_1,
  output [31:0] Data_In_2,
  output [31:0] Data_In_3,
  output [15:0] Address,
  output [3:0] mask
);

  Multiplexer #(.select(2), .width(4)) multiplexer_1 (
    .in0(4'b0001), .in1(4'b0010), .in2(4'b0100), .in3(4'b1000), .out(mask), .sel(Address_In[3:2]));  // open: en

  assign Address = Address_In[19:4];
  assign Data_In_0 = {Data_In[7:0], Data_In[15:8], Data_In[23:16], Data_In[31:24]};
  assign Data_In_1 = {Data_In[7:0], Data_In[15:8], Data_In[23:16], Data_In[31:24]};
  assign Data_In_2 = {Data_In[7:0], Data_In[15:8], Data_In[23:16], Data_In[31:24]};
  assign Data_In_3 = {Data_In[7:0], Data_In[15:8], Data_In[23:16], Data_In[31:24]};

  // Other names for the same wires on the sheet: offSet[1:0] = Address_In[3:2]
endmodule

module MemoryReaderNOI (
  input  [31:0] Address_To_Read,
  output [15:0] Address,
  output [1:0] OffSet
);


  assign Address = Address_To_Read[19:4];
  assign OffSet = Address_To_Read[3:2];
endmodule
